# Fritzing sketch squaresynth-step0 (saved by Fritzing 0.9.0b)
circuit board: 8.46667cm x 5.64444cm
breadboards: 1

parts:
  BAT1 = BC9VPC [package=bc9vpc]
  LED1 = LED - 5mm [color="White (4500K)" package="5 mm [THT]"]
  R7 = Resistor [tolerance=±5% resistance=1k package=THT]

nets:
  N1: BAT1.V+, LED1.anode
  N2: BAT1.V-, R7.Pin_1
  N3: LED1.cathode, R7.Pin_0
