# Fritzing sketch squaresynth-step1 (saved by Fritzing 0.9.0b)
circuit board: 8.46667cm x 5.64444cm
breadboards: 1

parts:
  R4 = Resistor [tolerance=±5% resistance=1k package=THT]
  C1 = Electrolytic Capacitor [capacitance=22pF package="100 mil [THT, electrolytic]"]
  BAT1 = BC9VPC [package=bc9vpc]
  BC1 = CD4093 [part_number=CD4093BC package="DIP14 [THT]"]
  AMP+SPKR1 = Loudspeaker
  LED1 = LED - 5mm [color="White (4500K)" package="5 mm [THT]"]
  R7 = Resistor [tolerance=±5% resistance=1k package=THT]

nets:
  N1: R4.Pin_0, BC1.L
  N2: R4.Pin_1, C1.+, BC1.E, AMP+SPKR1.pin2
  N3: C1.-, BAT1.V-, BC1.GND, AMP+SPKR1.pin1, R7.Pin_1
  N4: BAT1.V+, BC1.VCC, LED1.anode
  N5: BC1.A, BC1.H
  N6: BC1.J, BC1.C
  N7: BC1.F, BC1.M
  N8: LED1.cathode, R7.Pin_0

custom parts:
  CD4093: Quad NAN Schmitt Trigger
