# Fritzing sketch squaresynth-step3 (saved by Fritzing 0.9.0b)
circuit board: 8.46667cm x 5.64444cm
breadboards: 1

parts:
  R4 = Resistor [tolerance=±5% resistance=1k package=THT]
  C3 = Ceramic Capacitor [capacitance=2.2µF package="100 mil [THT, multilayer]"]
  R5 = Rotary Potentiometer (Small) [maximum_resistance=200kΩ package=THT]
  D1 = Rectifier Diode [part_number=1N4001 package="300 mil [THT]"]
  C1 = Electrolytic Capacitor [capacitance=22pF package="100 mil [THT, electrolytic]"]
  BAT1 = BC9VPC [package=bc9vpc]
  BC1 = CD4093 [part_number=CD4093BC package="DIP14 [THT]"]
  SPKR1 = Loudspeaker
  LED1 = LED - 5mm [color="White (4500K)" package="5 mm [THT]"]
  R7 = Resistor [tolerance=±5% resistance=1k package=THT]

nets:
  N1: R4.Pin_0, D1.anode, BC1.L
  N2: R4.Pin_1, C1.+, BC1.E
  N3: C3.0, R5.leg1, BC1.G
  N4: C3.1, C1.-, BAT1.V-, BC1.GND, SPKR1.pin1, R7.Pin_1
  N5: R5.wiper, BC1.F, BC1.M
  N6: D1.cathode, SPKR1.pin2
  N7: BAT1.V+, BC1.VCC, LED1.anode
  N8: BC1.A, BC1.H
  N9: BC1.J, BC1.C
  N10: LED1.cathode, R7.Pin_0

custom parts:
  CD4093: Quad NAN Schmitt Trigger
